# Fritzing sketch receiver plotter (saved by Fritzing 0.8.3b)

parts:
  Part1 = Arduino Uno (Rev3)  # not connected
  Part2 = Arduino XBee Shield
  U1 = XBee  # not connected
  J1 = Basic Servo
  J2 = Power Jack [package=power_jack_pth_lock]

nets:
  N1: Part2.D9, J1.pulse
  N2: Part2.GND, J2.GNDBREAK
  GND: J1.gnd, J2.GND
  N3: J1.vcc, J2.PWR
