# Fritzing sketch transmitter sensor (saved by Fritzing 0.8.3b)

parts:
  LCD1 = LCD screen
  Part7 = Arduino Uno (Rev3)
  R1 = Rotary Potentiometer (Small)
  Part8 = Arduino XBee Shield
  U1 = XBee  # not connected
  U2 = GAS_SENSOR [package=mq-3]
  R2 = Resistor [tolerance=±5% resistance=220 package=THT]

nets:
  VSS: LCD1.VSS, LCD1.LED-, Part7.GND, R1.leg2
  VDD: LCD1.VDD, LCD1.LED+, R1.leg1, Part8.5V, U2.H1
  N1: LCD1.V0, R1.wiper
  N2: LCD1.RS, Part7.ICSP_MISO, Part7.D12/MISO
  N3: LCD1.E, Part7.ICSP_MOSI, Part7.D11_PWM/MOSI
  N4: LCD1.DB4, Part7.D5_PWM
  N5: LCD1.DB5, Part7.D4
  N6: LCD1.DB6, Part7.D3_PWM
  N7: LCD1.DB7, Part7.D2
  N8: Part8.A0, U2.B1, R2.Pin_0
  N9: Part8.GND, U2.A1, R2.Pin_1

notes:
  10 k resistor
  10 k Pot
  MQ7 CO sensor
